# Fritzing sketch ESP32 CAM schematics (saved by Fritzing 0.9.9b)
breadboards: 1

parts:
  ESP32_-_Front1 = ESP32 - CAM
  Part1 = FTDI Basic Programmer
  S1 = Pushbutton [package=THT]

nets:
  N1: ESP32_-_Front1.GND#7, Part1.GND
  N2: ESP32_-_Front1.5V, Part1.POWER
  N3: ESP32_-_Front1.GPIO0, S1.leg1
  N4: ESP32_-_Front1.GND#12, S1.leg0
  N5: ESP32_-_Front1.GPIO3_/_RX, Part1.TXO
  N6: ESP32_-_Front1.GPIO1_/_TX, Part1.RXI

custom parts:
  ESP32 - CAM: The ESP32-CAM has a very competitive small-size camera module that can operate independently as a minimum system with a footprint of only 27*40.5*4.5mm and a deep sleep current of up to 6mA.
  FTDI Basic Programmer: Description: This is the newest revision of our FTDI Basic. We now use a SMD 6-pin header on the bottom, which makes it smaller and more compact. Functionality has remained the same. This is a basic breakout board for the FTDI FT232RL USB to serial IC. The pinout of this board matches the FTDI cable to work with official Arduino and cloned 3.3V Arduino boards. It can also be used for general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
