# Fritzing sketch esp32 toggle schematics (saved by Fritzing 0.9.9b)

parts:
  U1 = RELAY-SOLIDSTATE [package=relay-s108t02]
  Power_plug1 = Power plug
  U3 = ESP32-WROOM-32D-NodeMCU
  LED1 = LEDs [package=led10mm]

nets:
  N1: U1.T1, Power_plug1.VCC
  N2: U1.T2, LED1.C
  N3: U1.+, U3.G23
  N4: U1.-, U3.GND
  N5: Power_plug1.GND, LED1.A

custom parts:
  LEDs: LEDs Standard schematic elements and footprints for 5mm, 3mm, 1206, and 0603 sized LEDs. 5mm - Spark Fun Electronics SKU : COM-00529 (and others)
