# Fritzing sketch RFID reader schematics (saved by Fritzing 0.9.9b)
breadboards: 1

parts:
  Part1 = RFID-RC522-v2
  U1 = ESP32-WROOM-32D-NodeMCU
  R1 = Resistor [tolerance=±5% resistance=330 package="2512 [SMD]"]
  R2 = Resistor [tolerance=±5% resistance=330 package="2512 [SMD]"]
  R3 = Resistor [tolerance=±5% resistance=330 package="2512 [SMD]"]
  LED1 = RGB LED (com. cathode, rbg) [package="5 mm [THT]"]  # not connected

nets:
  N1: Part1.SDA, U1.G0
  N2: Part1.SCK, U1.G4
  N3: Part1.MOSI, U1.G23
  N4: Part1.MISO, U1.G16
  GND: Part1.GND, U1.GND
  N5: Part1.RST, U1.G27
  3.3V: Part1.3.3V, U1.5V
  N6: U1.G33, R2.Pin_1
  N7: U1.G25, R3.Pin_1
  N8: U1.G26, R1.Pin_1
  N9: U1.SD1, U1.RXD

custom parts:
  RFID-RC522-v2: A simple China made RFID-RC522 Reader; do check the pin labels, as this is a MFRC522 based clone.
