# Fritzing sketch temperature and humidity sensor (saved by Fritzing 0.9.9b)
breadboards: 1

parts:
  RHT1 = Humidity and Temperature Sensor RHT03
  U1 = ESP32-WROOM-32D-NodeMCU
  R1 = Resistor [tolerance=±5% resistance=330 package="2010 [SMD]"]

nets:
  VCC: RHT1.Vcc, U1.5V, R1.Pin_1
  N1: RHT1.Data-signal, U1.G23, R1.Pin_0
  N2: RHT1.GND_1, U1.GND
